// Logisim project minirv.circ as structural Verilog: 3 circuits, main circuit minirv
module minirv (
);

  // GPR_32x32bit gpr_32x32bit_1: pin names not known
endmodule

module instruction_decoder (
  input  [31:0] in_1
);
endmodule

module addi_decoder (
  input  [31:0] opcode,
  output [4:0] rd,
  output [4:0] rs1,
  output [11:0] imm
);


  assign imm = opcode[31:20];
  assign rd = opcode[11:7];
  assign rs1 = opcode[19:15];
endmodule
